// Logisim project bridge controller 2.0.circ as structural Verilog: 1 circuit, main circuit main
module main (
  input  in_1,
  input  in_2,
  input  in_3,
  input  in_4,
  input  in_5
);

  wire and_1_out, and_2_out, or_1_out, or_2_out, xnor_1_out, xor_1_out;

  or or_1 (or_1_out, in_4, in_3, in_2, in_1);
  and and_1 (and_1_out, in_1, in_2, in_3, in_4);
  ExactlyOne xor_1 (.out(xor_1_out), .in0(in_1), .in1(in_2), .in2(in_3), .in3(in_4));
  and and_2 (and_2_out, or_1_out, xor_1_out, and_1_out);
  LED car_and_ship (.in(xnor_1_out));
  xnor xnor_1 (xnor_1_out, and_2_out, in_5);
  or or_2 (or_2_out, and_2_out, in_5);
  LED bridge (.in(or_2_out));
endmodule
